# Fritzing sketch Fritzing_Schematics (saved by Fritzing 0.9.5d)
circuit board: 8.21171cm x 7.67205cm

parts:
  A1 = Raspberry Pi 5
  M1 = MakerFocus MAX30102
  Power_plug1 = Power plug
  Part1 = HX711 Weighing Sensor Module
  U1 = TRANSCHIPTC5747 [package=camera_sfv24r-2st_2]
  Part2 = Adafruit VL530X Time of Flight Distance Sensor [part_number="Adafruit #3317"]
  hc-sr1 = hc-sr04  # not connected
  U2 = MLX90614 [package=to-39]  # not connected

nets:
  3V3: A1.3V3, M1.VIN
  VCC: A1.5V, Part1.VCC, Part2.VCC
  N1: A1.GPIO2, M1.SDA
  N2: A1.GPIO3, M1.SCL
  GND: A1.GND, M1.GND, Power_plug1.GND, Part1.GND, U1.DOUT_6, Part2.GND
  RXD/TXD: A1.GPIO10, A1.GPIO8, Part1.DO/RX, Part1.CK/TX
  N3: A1.GPIO5, Part2.SCL
  N4: A1.GPIO6, Part2.SDA
  N5: A1.BAT+, Power_plug1.VCC

custom parts:
  Raspberry Pi 5: The RPi5, a faster version of the awesome Raspberry Pi4B ARM Board with 40 pin gpio.
  MakerFocus MAX30102: Oximeter module using the MAX30102 chip. As usual, if you want the mounting holes in pcb, you need to drag a hole over the pad in silkscreen to actually drill the hole (by default they are not drilled)
  Adafruit VL530X Time of Flight Distance Sensor: The VL53L0X is a Time of Flight distance sensor like no other you've used! The sensor contains a very tiny invisible laser source, and a matching sensor. The VL53L0X can detect the "time of flight", or how long the light has taken to bounce back to the sensor. Since it uses a very narrow light source, it is good for determining distance of only the surface directly in front of it. Unlike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
